# Fritzing sketch BatteryCharger (saved by Fritzing 0.9.3b)
breadboards: 1

parts:
  Q1 = pnp-Powertransistor [part_number=BD676 package="TO220 [THT]"]
  LED1 = LEDs [package=led-0603]
  R1 = Resistor [tolerance=±5% resistance=1k package=THT]
  R2 = Resistor [tolerance=±5% resistance=2.7 package=THT]
  R3 = Resistor [tolerance=±5% resistance=10k package=THT]
  D1 = Schottky Diode [part_number=1N5817 package="300 mil [THT]"]
  Q3 = pnp-Powertransistor [part_number=BD676 package="TO220 [THT]"]
  Q4 = NPN-Transistor [package="TO92 [THT]"]
  LED2 = LEDs [package=led-0603]
  R4 = Resistor [tolerance=±5% resistance=1k package=THT]
  J1 = Power Jack [package=power_jack_pth_lock]
  D2 = Rectifier Diode [part_number=1N4001 package="300 mil [THT]"]
  J2_(Battery_9_6v_NiMH) = Screw terminal - 2 pins [package=THT]
  Q5 = NPN-Transistor [package="TO92 [THT]"]
  R5 = Resistor [tolerance=±5% resistance=2.2k package=THT]
  LED3 = LEDs [package=led-0603]
  R6 = Resistor [tolerance=±5% resistance=22k package=THT]
  U1 = LM 358 Dual Op-Amp [package="DIP8 [THT]"]
  R7 = Resistor [tolerance=±5% resistance=15k package=THT]
  R9 = Resistor [tolerance=±5% resistance=15k package=THT]
  R10 = Resistor [tolerance=±5% resistance=8.2k package=THT]
  R11 = Resistor [tolerance=±5% resistance=8.2k package=THT]
  R12 = Trimmer Potentiometer [maximum_resistance=10kΩ package=THT]
  R13 = Resistor [tolerance=±5% resistance=10k package=THT]

nets:
  N1: Q1.base, LED1.C, R1.Pin_1
  N2: Q1.collector, D1.anode
  N3: Q1.emitter, R2.Pin_0
  N4: LED1.A, R2.Pin_1, Q3.emitter, LED2.A, J1.PWR, R5.Pin_1
  N5: R1.Pin_0, Q4.C
  N6: R3.Pin_0, U1.connector0, R13.Pin_1
  N7: R3.Pin_1, Q4.B
  N8: D1.cathode, D2.cathode, J2_(Battery_9_6v_NiMH).pin1, R10.Pin_1
  N9: Q3.base, LED2.C, R4.Pin_1
  N10: Q3.collector, D2.anode
  GND: Q4.E, R4.Pin_0, J1.GND, J2_(Battery_9_6v_NiMH).pin2, Q5.E, U1.connector3, R9.Pin_0, R11.Pin_0
  N11: Q5.B, R6.Pin_0
  N12: Q5.C, LED3.C
  N13: R5.Pin_0, LED3.A
  N14: U1.connector1, R12.wiper
  N15: U1.connector2, U1.connector4, R7.Pin_0, R9.Pin_1, R13.Pin_0
  N16: U1.connector5, U1.connector6
  N17: U1.connector7, R7.Pin_1
  N18: R10.Pin_0, R12.leg2
  N19: R11.Pin_1, R12.leg1
