# Fritzing sketch Daddelkiste (saved by Fritzing 0.9.3b)
stripboards: 1

parts:
  Bauteil1 = Arduino Leonardo (Rev3b)
  IC1 = MICROCONTROLLER [part_number=Atmega8 package=dil28-3-zif_socket]
  U1 = LCD-16X2 [package=lcd-16x2_noholes]
  R1 = Resistor [tolerance=±5% resistance=10k package=THT]
  5V_from_Converter = USB Connectors [package=usb-mb-h]
  C1 = Ceramic Capacitor [capacitance="100 nF" package="0603 [SMD, multilayer]"]
  On/Off_Switch = Round Pushbutton
  R2 = Resistor [tolerance=±5% resistance=33 package=THT]
  Raspberry_Pi_2 = Raspberry Pi 4 [part_number=RPI-4-b]
  R3 = Resistor [tolerance=±5% resistance=68k package=THT]
  R4 = Resistor [tolerance=±5% resistance=47k package=THT]
  Power_plug1 = Power plug
  JP1 = Header 5x2 [package=avr_icsp]
  R5 = Resistor [tolerance=±5% resistance=2.2k package=THT]
  R7 = Resistor [tolerance=±5% resistance=2.2k package=THT]
  Q1 = NPN-Transistor [package="TO92 [THT]"]
  R8 = Resistor [tolerance=±5% resistance=10k package=THT]
  Fan_Connecter = screw terminal, 2 pins
  D1 = Rectifier Diode [part_number=1N4001 package="300 mil [THT]"]
  C2 = Electrolytic Capacitor [capacitance=10µF package="100 mil [THT, electrolytic]"]
  D2 = Rectifier Diode [part_number=1N4001 package="300 mil [THT]"]
  C3 = Electrolytic Capacitor [capacitance=100µF package="100 mil [THT, electrolytic]"]
  Volume = Rotary Potentiometer (Large) [maximum_resistance=10kΩ package=THT]
  R9_(Contrast) = Trimmer Potentiometer [maximum_resistance=22kΩ package=THT]

nets:
  N1: Bauteil1.D3_PWM/SCL, Bauteil1.SCL, IC1.PC5(ADC5_SCL), R5.Pin_0
  N2: Bauteil1.D6_PWM/A7, C2.+
  N3: Bauteil1.D7, IC1.PC6(_RESET), R1.Pin_0, JP1.5
  5V: Bauteil1.5V, U1.VDD, R2.Pin_0, Volume.leg2
  GND: Bauteil1.GND, IC1.GND, IC1.AGND, U1.VSS, U1.R_W, U1.K, 5V_from_Converter.GND, C1.0, On/Off_Switch.leg1, Raspberry_Pi_2.GND, R4.Pin_1, Power_plug1.GND, JP1.4, JP1.6, JP1.8, JP1.10, Q1.E, D1.cathode, C3.+, Volume.leg1, R9_(Contrast).leg2
  N4: Bauteil1.A0, Volume.wiper
  N5: Bauteil1.A2, U1.DB4
  N6: Bauteil1.A3, U1.DB5
  N7: Bauteil1.A4, U1.DB6
  N8: Bauteil1.A5, U1.DB7
  N9: Bauteil1.D9_PWM/A9, Q1.B, R8.Pin_0, R8.Pin_1
  N10: Bauteil1.D11_PWM, U1.E
  N11: Bauteil1.D12/A11, U1.RS
  N12: Bauteil1.SDA, IC1.PC4(ADC4_SDA), R7.Pin_0
  N13: IC1.PD2(INT0), On/Off_Switch.leg0
  N14: IC1.VCC, IC1.AVCC, R1.Pin_1, 5V_from_Converter.D+, JP1.2, R5.Pin_1, R7.Pin_1
  N15: IC1.PB0(ICP), Raspberry_Pi_2.GLOBAL_EN
  N16: IC1.PB1(OC1A), Raspberry_Pi_2.GPIO17
  N17: IC1.PB3(MOSI_OC2), JP1.1
  N18: IC1.PB5(SCK), JP1.7
  N19: IC1.AREF, C1.1
  3V3: IC1.PC0(ADC0), Raspberry_Pi_2.3v3, Raspberry_Pi_2.3V3
  N20: IC1.PC1(ADC1), R3.Pin_0, R4.Pin_0
  N21: U1.VO, R9_(Contrast).wiper
  N22: U1.A, R2.Pin_1
  N23: R3.Pin_1, Power_plug1.VCC, Fan_Connecter.pin2
  N24: Q1.C, Fan_Connecter.pin1
  N25: D1.anode, C2.-, D2.cathode
  N26: D2.anode, C3.-, R9_(Contrast).leg1

custom parts:
  Raspberry Pi 4: The RPi4, a faster version of the awesome Raspberry Pi 2 B ARM Board with 40 pin gpio. Ready for special Raspberry Pi B+ and RPi2 Hat (Hardware attached (on) top)
